// Logisim project cpu_p3.circ as structural Verilog: 18 circuits, main circuit main
module main (
  input  reset,
  output [31:0] Instr,
  output [31:0] PC,
  output RegWrite,
  output [4:0] RegAddr,
  output [31:0] RegData,
  output MemWrite,
  output [31:0] MemAddr,
  output [31:0] MemData
);

  wire ALU2Reg, alu_1_eq, alu_1_gt, alu_1_lt, ALUimm, beq, clk, controller_1_savert, imm2Reg, jflag, Mem2Reg,
       MemLoad;
  wire [1:0] ALUop;
  wire [4:0] controller_1_rd, controller_1_rs, controller_1_rt, muxgrfaddr_1_grfaddrout1,
       muxgrfaddr_1_grfaddrout2;
  wire [5:0] func, op;
  wire [15:0] addr16;
  wire [25:0] addr26;
  wire [31:0] ALUout, MemOut, muxalu_1_operand1, muxalu_1_operand2, RsOut;

  Clock clock_1 (.out(clk));
  IFU ifu_1 (.offset(addr16), .jflag(jflag), .PC(PC), .clk(clk), .reset(reset), .instruct(Instr));
  Mux2Reg mux2reg_1 (
    .ALUout(ALUout), .ALU2Reg(ALU2Reg), .Memout(MemOut), .Mem2Reg(Mem2Reg), .immout(addr16),
    .imm2Reg(imm2Reg), .out_7(RegData));
  Controller controller_1 (
    .\input (Instr), .op(op), .Rs(controller_1_rs), .Rt(controller_1_rt), .Rd(controller_1_rd), .func(func),
    .addr16(addr16), .addr26(addr26), .ALUop(ALUop), .RegWrite(RegWrite), .MemWrite(MemWrite),
    .MemLoad(MemLoad), .ALU2Reg(ALU2Reg), .Mem2Reg(Mem2Reg), .imm2Reg(imm2Reg), .beq(beq),
    .saveRt(controller_1_savert), .ALUimm(ALUimm));  // open: Shamt
  MuxGRFAddr muxgrfaddr_1 (
    .Rd(controller_1_rd), .Rs(controller_1_rs), .Rt(controller_1_rt), .saveRt(controller_1_savert),
    .GFRAddrIn(RegAddr), .GRFAddrOut1(muxgrfaddr_1_grfaddrout1), .GRFAddrOut2(muxgrfaddr_1_grfaddrout2));
  GRF grf_1 (
    .RegWrite(RegWrite), .RegData(RegData), .RegAddrIn(RegAddr), .AddrOut1(muxgrfaddr_1_grfaddrout1),
    .AddrOut2(muxgrfaddr_1_grfaddrout2), .clk(clk), .in_7(reset), .Out1(RsOut), .Out2(MemData));
  DM dm_1 (
    .base(RsOut), .offset(addr16), .\input (MemData), .MemAddr(MemAddr), .MemWrite(MemWrite), .clk(clk),
    .MemLoad(MemLoad), .reset(reset), .\output (MemOut));
  MuxALU muxalu_1 (
    .Rs(RsOut), .Rt(MemData), .imm(addr16), .ALUimm(ALUimm), .Operand1(muxalu_1_operand1),
    .Operand2(muxalu_1_operand2));
  ALU alu_1 (
    .op(ALUop), .operand1(muxalu_1_operand1), .operand2(muxalu_1_operand2), .ALUout(ALUout), .gt(alu_1_gt),
    .eq(alu_1_eq), .lt(alu_1_lt));
  comp2jflag comp2jflag_1 (.beq(beq), .gt(alu_1_gt), .eq(alu_1_eq), .lt(alu_1_lt), .jflag(jflag));

  // Other names for the same wires on the sheet: MemIn[31:0] = MemData; RtOut[31:0] = MemData
endmodule

module ALU (
  input  [1:0] op,
  input  [31:0] operand1,
  input  [31:0] operand2,
  output [31:0] ALUout,
  output gt,
  output eq,
  output lt
);

  wire [31:0] add, \or , sub;

  Adder #(.width(32)) adder_1 (.a(operand1), .b(operand2), .out(add));  // open: cin, cout
  Subtractor #(.width(32)) subtractor_1 (.a(operand1), .b(operand2), .out(sub));  // open: bin, bout
  assign \or  = operand1 | operand2;  // OR_Gate or_1, 32 bits wide
  Comparator #(.width(32)) comparator_1 (.a(operand1), .b(operand2), .gt(gt), .eq(eq), .lt(lt));
  Multiplexer #(.select(2), .width(32)) multiplexer_1 (
    .in0(add), .in1(sub), .in2(\or ), .out(ALUout), .sel(op));  // open: in3, en
endmodule

module GRF (
  input  RegWrite,
  input  [31:0] RegData,
  input  [4:0] RegAddrIn,
  input  [4:0] AddrOut1,
  input  [4:0] AddrOut2,
  input  clk,
  input  in_7,
  output [31:0] Out1,
  output [31:0] Out2
);

  wire and_2_out, and_3_out, and_4_out, and_5_out, and_6_out, and_7_out, and_8_out, and_9_out, and_10_out,
       and_11_out, and_12_out, and_13_out, and_14_out, and_15_out, and_16_out, and_17_out, and_18_out,
       and_19_out, and_20_out, and_21_out, and_22_out, and_23_out, and_24_out, and_25_out, and_26_out,
       and_27_out, and_28_out, and_29_out, and_30_out, and_31_out, and_32_out, c1, c2, c3, c4, r1, r2, r3,
       r4, r5, r6, r7, r8;
  wire [4:0] and_1_out, bit_extender_1_out;
  wire [31:0] out1_t, out2_t, out3, out4, out5, out6, out7, out8, out9, out10, out11, out12, out13, out14,
       out15, out16, out17, out18, out19, out20, out21, out22, out23, out24, out25, out26, out27, out28,
       out29, out30, out31;

  assign and_1_out = RegAddrIn & bit_extender_1_out;  // AND_Gate and_1, 5 bits wide
  assign bit_extender_1_out = {{4{RegWrite}}, RegWrite};  // Bit_Extender bit_extender_1
  Decoder #(.select(3)) decoder_1 (
    .out0(r1), .out1(r2), .out2(r3), .out3(r4), .out4(r5), .out5(r6), .out6(r7), .out7(r8),
    .sel(and_1_out[2:0]));  // open: en
  Decoder #(.select(2)) decoder_2 (.out0(c1), .out1(c2), .out2(c3), .out3(c4), .sel(and_1_out[4:3]));  // open: en
  and and_2 (and_2_out, r2, c1);
  and and_3 (and_3_out, r3, c1);
  and and_4 (and_4_out, r4, c1);
  and and_5 (and_5_out, r5, c1);
  and and_6 (and_6_out, r6, c1);
  and and_7 (and_7_out, r7, c1);
  and and_8 (and_8_out, r8, c1);
  Register #(.width(32)) register_1 (.D(RegData), .en(and_2_out), .Q(out1_t), .clk(clk), .clr(in_7));
  Register #(.width(32)) register_2 (.D(RegData), .en(and_3_out), .Q(out2_t), .clk(clk), .clr(in_7));
  Register #(.width(32)) register_3 (.D(RegData), .en(and_4_out), .Q(out3), .clk(clk), .clr(in_7));
  Register #(.width(32)) register_4 (.D(RegData), .en(and_5_out), .Q(out4), .clk(clk), .clr(in_7));
  Register #(.width(32)) register_5 (.D(RegData), .en(and_6_out), .Q(out5), .clk(clk), .clr(in_7));
  Register #(.width(32)) register_6 (.D(RegData), .en(and_7_out), .Q(out6), .clk(clk), .clr(in_7));
  Register #(.width(32)) register_7 (.D(RegData), .en(and_8_out), .Q(out7), .clk(clk), .clr(in_7));
  and and_9 (and_9_out, r1, c2);
  and and_10 (and_10_out, r2, c2);
  and and_11 (and_11_out, r3, c2);
  and and_12 (and_12_out, r4, c2);
  and and_13 (and_13_out, r5, c2);
  and and_14 (and_14_out, r6, c2);
  and and_15 (and_15_out, r7, c2);
  and and_16 (and_16_out, r8, c2);
  Register #(.width(32)) register_8 (.D(RegData), .en(and_9_out), .Q(out8), .clk(clk), .clr(in_7));
  Register #(.width(32)) register_9 (.D(RegData), .en(and_10_out), .Q(out9), .clk(clk), .clr(in_7));
  Register #(.width(32)) register_10 (.D(RegData), .en(and_11_out), .Q(out10), .clk(clk), .clr(in_7));
  Register #(.width(32)) register_11 (.D(RegData), .en(and_12_out), .Q(out11), .clk(clk), .clr(in_7));
  Register #(.width(32)) register_12 (.D(RegData), .en(and_13_out), .Q(out12), .clk(clk), .clr(in_7));
  Register #(.width(32)) register_13 (.D(RegData), .en(and_14_out), .Q(out13), .clk(clk), .clr(in_7));
  Register #(.width(32)) register_14 (.D(RegData), .en(and_15_out), .Q(out14), .clk(clk), .clr(in_7));
  Register #(.width(32)) register_15 (.D(RegData), .en(and_16_out), .Q(out15), .clk(clk), .clr(in_7));
  and and_17 (and_17_out, r1, c3);
  and and_18 (and_18_out, r2, c3);
  and and_19 (and_19_out, r3, c3);
  and and_20 (and_20_out, r4, c3);
  and and_21 (and_21_out, r5, c3);
  and and_22 (and_22_out, r6, c3);
  and and_23 (and_23_out, r7, c3);
  and and_24 (and_24_out, r8, c3);
  Register #(.width(32)) register_16 (.D(RegData), .en(and_17_out), .Q(out16), .clk(clk), .clr(in_7));
  Register #(.width(32)) register_17 (.D(RegData), .en(and_18_out), .Q(out17), .clk(clk), .clr(in_7));
  Register #(.width(32)) register_18 (.D(RegData), .en(and_19_out), .Q(out18), .clk(clk), .clr(in_7));
  Register #(.width(32)) register_19 (.D(RegData), .en(and_20_out), .Q(out19), .clk(clk), .clr(in_7));
  Register #(.width(32)) register_20 (.D(RegData), .en(and_21_out), .Q(out20), .clk(clk), .clr(in_7));
  Register #(.width(32)) register_21 (.D(RegData), .en(and_22_out), .Q(out21), .clk(clk), .clr(in_7));
  Register #(.width(32)) register_22 (.D(RegData), .en(and_23_out), .Q(out22), .clk(clk), .clr(in_7));
  Register #(.width(32)) register_23 (.D(RegData), .en(and_24_out), .Q(out23), .clk(clk), .clr(in_7));
  and and_25 (and_25_out, r1, c4);
  and and_26 (and_26_out, r2, c4);
  and and_27 (and_27_out, r3, c4);
  and and_28 (and_28_out, r4, c4);
  and and_29 (and_29_out, r5, c4);
  and and_30 (and_30_out, r6, c4);
  and and_31 (and_31_out, r7, c4);
  and and_32 (and_32_out, r8, c4);
  Register #(.width(32)) register_24 (.D(RegData), .en(and_25_out), .Q(out24), .clk(clk), .clr(in_7));
  Register #(.width(32)) register_25 (.D(RegData), .en(and_26_out), .Q(out25), .clk(clk), .clr(in_7));
  Register #(.width(32)) register_26 (.D(RegData), .en(and_27_out), .Q(out26), .clk(clk), .clr(in_7));
  Register #(.width(32)) register_27 (.D(RegData), .en(and_28_out), .Q(out27), .clk(clk), .clr(in_7));
  Register #(.width(32)) register_28 (.D(RegData), .en(and_29_out), .Q(out28), .clk(clk), .clr(in_7));
  Register #(.width(32)) register_29 (.D(RegData), .en(and_30_out), .Q(out29), .clk(clk), .clr(in_7));
  Register #(.width(32)) register_30 (.D(RegData), .en(and_31_out), .Q(out30), .clk(clk), .clr(in_7));
  Register #(.width(32)) register_31 (.D(RegData), .en(and_32_out), .Q(out31), .clk(clk), .clr(in_7));
  Multiplexer #(.select(5), .width(32)) multiplexer_1 (
    .in0({32{1'b0}}), .in1(out1_t), .in2(out2_t), .in3(out3), .in4(out4), .in5(out5), .in6(out6), .in7(out7),
    .in8(out8), .in9(out9), .in10(out10), .in11(out11), .in12(out12), .in13(out13), .in14(out14),
    .in15(out15), .in16(out16), .in17(out17), .in18(out18), .in19(out19), .in20(out20), .in21(out21),
    .in22(out22), .in23(out23), .in24(out24), .in25(out25), .in26(out26), .in27(out27), .in28(out28),
    .in29(out29), .in30(out30), .in31(out31), .out(Out1), .sel(AddrOut1));  // open: en
  Multiplexer #(.select(5), .width(32)) multiplexer_2 (
    .in0({32{1'b0}}), .in1(out1_t), .in2(out2_t), .in3(out3), .in4(out4), .in5(out5), .in6(out6), .in7(out7),
    .in8(out8), .in9(out9), .in10(out10), .in11(out11), .in12(out12), .in13(out13), .in14(out14),
    .in15(out15), .in16(out16), .in17(out17), .in18(out18), .in19(out19), .in20(out20), .in21(out21),
    .in22(out22), .in23(out23), .in24(out24), .in25(out25), .in26(out26), .in27(out27), .in28(out28),
    .in29(out29), .in30(out30), .in31(out31), .out(Out2), .sel(AddrOut2));  // open: en

  // Other names for the same wires on the sheet: reset = in_7
endmodule

module op2command (
  input  op5,
  input  op4,
  input  op3,
  input  op2,
  input  op1,
  input  op0,
  output add,
  output sub,
  output ori,
  output lw,
  output sw,
  output beq,
  output lui
);

  wire not_1_out, not_2_out, not_3_out, not_4_out, not_5_out, not_6_out;

  not not_1 (not_1_out, op4);
  not not_2 (not_2_out, op5);
  not not_3 (not_3_out, op3);
  not not_4 (not_4_out, op2);
  not not_5 (not_5_out, op1);
  not not_6 (not_6_out, op0);
  and and_1 (add, not_2_out, not_1_out, not_3_out, not_4_out, not_5_out, not_6_out);
  and and_2 (sub, not_2_out, not_1_out, not_3_out, not_4_out, not_5_out, not_6_out);
  and and_3 (ori, not_2_out, not_1_out, op3, op2, not_5_out, op0);
  and and_4 (lw, op5, not_1_out, not_3_out, not_4_out, op1, op0);
  and and_5 (sw, op5, not_1_out, op3, not_4_out, op1, op0);
  and and_6 (beq, not_2_out, not_1_out, not_3_out, op2, not_5_out, not_6_out);
  and and_7 (lui, not_2_out, not_1_out, op3, op2, op1, op0);
endmodule

module command2csig (
  input  add,
  input  sub,
  input  ori,
  input  lw,
  input  sw,
  input  beq,
  input  lui,
  output [1:0] ALUop,
  output RegWrite,
  output MemWrite,
  output MemLoad,
  output ALU2Reg,
  output Mem2Reg,
  output imm2Reg,
  output beq_2,
  output saveRt,
  output ALUimm
);

  or or_1 (RegWrite, add, sub, ori, lw, lui);
  or or_2 (ALU2Reg, add, sub, ori);
  or or_3 (saveRt, lui, lw, ori);

  assign ALUimm = ori;
  assign ALUop = {ori, sub};
  assign beq_2 = beq;
  assign imm2Reg = lui;
  assign Mem2Reg = lw;
  assign MemLoad = lw;
  assign MemWrite = sw;
endmodule

module func2command (
  input  f5,
  input  f4,
  input  f3,
  input  f2,
  input  f1,
  input  f0,
  output add,
  output sub
);

  wire not_1_out, not_2_out, not_3_out, not_4_out, not_5_out, not_6_out;

  not not_1 (not_1_out, f5);
  not not_2 (not_2_out, f4);
  not not_3 (not_3_out, f3);
  not not_4 (not_4_out, f2);
  not not_5 (not_5_out, f1);
  not not_6 (not_6_out, f0);
  and and_1 (add, f5, not_2_out, not_3_out, not_4_out, not_5_out, not_6_out);
  and and_2 (sub, f5, not_2_out, not_3_out, not_4_out, f1, not_6_out);
endmodule

module op_func2command (
  input  [5:0] op,
  input  [5:0] func,
  output add,
  output sub,
  output ori,
  output lw,
  output sw,
  output beq,
  output lui
);

  wire func2command_1_add, func2command_1_sub, op2command_1_add, op2command_1_sub;

  op2command op2command_1 (
    .op5(op[5]), .op4(op[4]), .op3(op[3]), .op2(op[2]), .op1(op[1]), .op0(op[0]), .add(op2command_1_add),
    .sub(op2command_1_sub), .ori(ori), .lw(lw), .sw(sw), .beq(beq), .lui(lui));
  func2command func2command_1 (
    .f5(func[5]), .f4(func[4]), .f3(func[3]), .f2(func[2]), .f1(func[1]), .f0(func[0]),
    .add(func2command_1_add), .sub(func2command_1_sub));
  and and_1 (add, op2command_1_add, func2command_1_add);
  and and_2 (sub, op2command_1_sub, func2command_1_sub);
endmodule

module instructAnalyser (
  input  [31:0] \input ,
  output [5:0] op,
  output [4:0] Rs,
  output [4:0] Rt,
  output [4:0] Rd,
  output [4:0] Shamt,
  output [5:0] func,
  output [15:0] addr16,
  output [25:0] addr26
);


  assign addr16 = \input [15:0];
  assign addr26 = \input [25:0];
  assign func = \input [5:0];
  assign op = \input [31:26];
  assign Rd = \input [15:11];
  assign Rs = \input [25:21];
  assign Rt = \input [20:16];
  assign Shamt = \input [10:6];
endmodule

module draft (
  input  reset
);

  wire alu_1_eq, alu_1_gt, alu_1_lt, clock_1_out, command2csig_1_alu2reg, command2csig_1_beq_2,
       command2csig_1_imm2reg, command2csig_1_mem2reg, command2csig_1_memload, command2csig_1_memwrite,
       comp2jflag_1_jflag, grf_1_p1, op_func2command_1_add, op_func2command_1_beq, op_func2command_1_lui,
       op_func2command_1_lw, op_func2command_1_ori, op_func2command_1_sub, op_func2command_1_sw;
  wire [1:0] command2csig_1_aluop;
  wire [4:0] instructanalyser_1_rd, instructanalyser_1_rs, instructanalyser_1_rt;
  wire [5:0] instructanalyser_1_func, instructanalyser_1_op;
  wire [15:0] base_offset2addr_1_addr, instructanalyser_1_addr16;
  wire [31:0] alu_1_aluout, grf_1_p3, grf_1_p8, grf_1_p9, ifu_1_instruct, ram_1_data;

  Clock clock_1 (.out(clock_1_out));
  IFU ifu_1 (
    .offset(instructanalyser_1_addr16), .jflag(comp2jflag_1_jflag), .clk(clock_1_out), .reset(reset),
    .instruct(ifu_1_instruct));  // open: PC
  instructAnalyser instructanalyser_1 (
    .\input (ifu_1_instruct), .op(instructanalyser_1_op), .Rs(instructanalyser_1_rs),
    .Rt(instructanalyser_1_rt), .Rd(instructanalyser_1_rd), .func(instructanalyser_1_func),
    .addr16(instructanalyser_1_addr16));  // open: Shamt, addr26
  op_func2command op_func2command_1 (
    .op(instructanalyser_1_op), .func(instructanalyser_1_func), .add(op_func2command_1_add),
    .sub(op_func2command_1_sub), .ori(op_func2command_1_ori), .lw(op_func2command_1_lw),
    .sw(op_func2command_1_sw), .beq(op_func2command_1_beq), .lui(op_func2command_1_lui));
  // GRF grf_1: pin names not known; wires that end beside it: grf_1_p1, instructanalyser_1_rd, grf_1_p3, instructanalyser_1_rs, instructanalyser_1_rt, clock_1_out, reset, grf_1_p8, grf_1_p9
  command2csig command2csig_1 (
    .add(op_func2command_1_add), .sub(op_func2command_1_sub), .ori(op_func2command_1_ori),
    .lw(op_func2command_1_lw), .sw(op_func2command_1_sw), .beq(op_func2command_1_beq),
    .lui(op_func2command_1_lui), .ALUop(command2csig_1_aluop), .RegWrite(grf_1_p1),
    .MemWrite(command2csig_1_memwrite), .MemLoad(command2csig_1_memload), .ALU2Reg(command2csig_1_alu2reg),
    .Mem2Reg(command2csig_1_mem2reg), .imm2Reg(command2csig_1_imm2reg), .beq_2(command2csig_1_beq_2));  // open: saveRt, ALUimm
  ALU alu_1 (
    .op(command2csig_1_aluop), .operand1(grf_1_p8), .operand2(grf_1_p9), .ALUout(alu_1_aluout),
    .gt(alu_1_gt), .eq(alu_1_eq), .lt(alu_1_lt));
  base_offset2addr base_offset2addr_1 (
    .base(grf_1_p8), .offset(instructanalyser_1_addr16), .addr(base_offset2addr_1_addr));
  comp2jflag comp2jflag_1 (
    .beq(command2csig_1_beq_2), .gt(alu_1_gt), .eq(alu_1_eq), .lt(alu_1_lt), .jflag(comp2jflag_1_jflag));
  Mux2Reg mux2reg_1 (
    .ALUout(alu_1_aluout), .ALU2Reg(command2csig_1_alu2reg), .Memout(ram_1_data),
    .Mem2Reg(command2csig_1_mem2reg), .immout(instructanalyser_1_addr16), .imm2Reg(command2csig_1_imm2reg),
    .out_7(grf_1_p3));
  RAM #(.addrWidth(16), .dataWidth(32), .bus("separate")) ram_1 (
    .addr(base_offset2addr_1_addr), .din(grf_1_p9), .data(ram_1_data), .str(command2csig_1_memwrite),
    .clk(clock_1_out), .ld(command2csig_1_memload));  // open: sel, clr
endmodule

module DM (
  input  [31:0] base,
  input  [15:0] offset,
  input  [31:0] \input ,
  input  MemWrite,
  input  reset,
  input  clk,
  input  MemLoad,
  output [31:0] MemAddr,
  output [31:0] \output 
);

  wire not_1_out;
  wire [15:0] base_offset2addr_1_addr, shifter_1_out;
  wire [31:0] ram_1_data;

  base_offset2addr base_offset2addr_1 (.base(base), .offset(offset), .addr(base_offset2addr_1_addr));
  Shifter #(.width(16), .shift("lr")) shifter_1 (.in(base_offset2addr_1_addr), .\dist (4'b0010), .out(shifter_1_out));
  assign MemAddr = {{16{1'b0}}, base_offset2addr_1_addr};  // Bit_Extender bit_extender_1
  RAM #(.addrWidth(16), .dataWidth(32), .bus("separate")) ram_1 (
    .addr(shifter_1_out), .din(\input ), .data(ram_1_data), .str(MemWrite), .clk(clk), .ld(MemLoad),
    .clr(reset));  // open: sel
  Multiplexer #(.width(32)) multiplexer_1 (
    .in0(ram_1_data), .in1({32{1'b0}}), .out(\output ), .sel(not_1_out));  // open: en
  not not_1 (not_1_out, MemLoad);
endmodule

module Mux2Reg (
  input  [31:0] ALUout,
  input  ALU2Reg,
  input  [31:0] Memout,
  input  Mem2Reg,
  input  [15:0] immout,
  input  imm2Reg,
  output [31:0] out_7
);

  wire [31:0] and_1_out, and_2_out, and_3_out, bit_extender_1_out, bit_extender_2_out, bit_extender_3_out,
       bit_extender_4_out, shifter_1_out;

  assign bit_extender_1_out = {{16{1'b0}}, immout};  // Bit_Extender bit_extender_1
  assign bit_extender_2_out = {{31{ALU2Reg}}, ALU2Reg};  // Bit_Extender bit_extender_2
  assign bit_extender_3_out = {{31{Mem2Reg}}, Mem2Reg};  // Bit_Extender bit_extender_3
  Shifter #(.width(32)) shifter_1 (.in(bit_extender_1_out), .\dist (5'b10000), .out(shifter_1_out));
  assign bit_extender_4_out = {{31{imm2Reg}}, imm2Reg};  // Bit_Extender bit_extender_4
  assign and_1_out = ALUout & bit_extender_2_out;  // AND_Gate and_1, 32 bits wide
  assign and_2_out = Memout & bit_extender_3_out;  // AND_Gate and_2, 32 bits wide
  assign and_3_out = shifter_1_out & bit_extender_4_out;  // AND_Gate and_3, 32 bits wide
  assign out_7 = and_1_out | and_2_out | and_3_out;  // OR_Gate or_1, 32 bits wide
endmodule

module IFU (
  input  [15:0] offset,
  input  jflag,
  input  clk,
  input  reset,
  output [31:0] PC,
  output [31:0] instruct
);

  wire counter_1_q, not_1_out;
  wire [15:0] bit_extender_2_out;
  wire [31:0] adder_1_out, adder_2_out, bit_extender_1_out, multiplexer_1_out, multiplexer_2_out,
       shifter_1_out, shifter_2_out, subtractor_1_out;

  assign bit_extender_1_out = {{16{offset[15]}}, offset};  // Bit_Extender bit_extender_1
  Multiplexer #(.width(32)) multiplexer_1 (
    .in0({32{1'b0}}), .in1(bit_extender_1_out), .out(multiplexer_1_out), .sel(jflag));  // open: en
  Adder #(.width(32)) adder_1 (.a(32'h4), .b(PC), .out(adder_1_out));  // open: cin, cout
  Shifter #(.width(32)) shifter_1 (.in(multiplexer_1_out), .\dist (5'b00010), .out(shifter_1_out));
  Adder #(.width(32)) adder_2 (.a(shifter_1_out), .b(adder_1_out), .out(adder_2_out));  // open: cin, cout
  not not_1 (not_1_out, counter_1_q);
  Counter #(.width(1), .max('h1), .ongoal("stay")) counter_1 (
    .Q(counter_1_q), .clk(clk), .clr(reset));  // open: load, D, count, carry
  Multiplexer #(.width(32)) multiplexer_2 (
    .in0(adder_2_out), .in1(32'h3000), .out(multiplexer_2_out), .sel(not_1_out));  // open: en
  Register #(.width(32)) u_PC (.D(multiplexer_2_out), .Q(PC), .clk(clk), .clr(reset));  // open: en
  Subtractor #(.width(32)) subtractor_1 (.a(PC), .b(32'h3000), .out(subtractor_1_out));  // open: bin, bout
  Shifter #(.width(32), .shift("lr")) shifter_2 (.in(subtractor_1_out), .\dist (5'b00010), .out(shifter_2_out));
  Bit_Extender #(.in_width(32)) bit_extender_2 (.in(shifter_2_out), .out(bit_extender_2_out));
  ROM #(.addrWidth(16), .dataWidth(32)) rom_1 (.addr(bit_extender_2_out), .data(instruct));  // open: sel

  // Notes on the sheet:
  //   contents of rom_1 (hex, n*v repeats v):
  //   341c0000 341d0000 34013456 210820 8c010004 ac010004 3c027878 411822 3c051234 34040005 0 ac85ffff
  //   8c83ffff 10650001 1000000d 34670404 10e3000b 0 3c087777 3508ffff 80022 34001100 e65020 34080000
  //   34090001 340a0001 10a4020 1109fffe 1000ffff
endmodule

module comp2jflag (
  input  gt,
  input  eq,
  input  lt,
  input  beq,
  output jflag
);

  and and_1 (jflag, beq, eq);
endmodule

module Controller (
  input  [31:0] \input ,
  output [1:0] ALUop,
  output RegWrite,
  output MemWrite,
  output MemLoad,
  output ALU2Reg,
  output Mem2Reg,
  output imm2Reg,
  output [5:0] op,
  output beq,
  output saveRt,
  output [4:0] Rs,
  output ALUimm,
  output [4:0] Rt,
  output [4:0] Rd,
  output [4:0] Shamt,
  output [5:0] func,
  output [15:0] addr16,
  output [25:0] addr26
);

  wire op_func2command_1_add, op_func2command_1_beq, op_func2command_1_lui, op_func2command_1_lw,
       op_func2command_1_ori, op_func2command_1_sub, op_func2command_1_sw;

  instructAnalyser instructanalyser_1 (
    .\input (\input ), .op(op), .Rs(Rs), .Rt(Rt), .Rd(Rd), .Shamt(Shamt), .func(func), .addr16(addr16),
    .addr26(addr26));
  op_func2command op_func2command_1 (
    .op(op), .func(func), .add(op_func2command_1_add), .sub(op_func2command_1_sub),
    .ori(op_func2command_1_ori), .lw(op_func2command_1_lw), .sw(op_func2command_1_sw),
    .beq(op_func2command_1_beq), .lui(op_func2command_1_lui));
  command2csig command2csig_1 (
    .add(op_func2command_1_add), .sub(op_func2command_1_sub), .ori(op_func2command_1_ori),
    .lw(op_func2command_1_lw), .sw(op_func2command_1_sw), .beq(op_func2command_1_beq),
    .lui(op_func2command_1_lui), .ALUop(ALUop), .RegWrite(RegWrite), .MemWrite(MemWrite), .MemLoad(MemLoad),
    .ALU2Reg(ALU2Reg), .Mem2Reg(Mem2Reg), .imm2Reg(imm2Reg), .beq_2(beq), .saveRt(saveRt), .ALUimm(ALUimm));
endmodule

module base_offset2addr (
  input  [31:0] base,
  input  [15:0] offset,
  output [15:0] addr
);

  wire [31:0] adder_1_out, bit_extender_1_out;

  assign bit_extender_1_out = {{16{offset[15]}}, offset};  // Bit_Extender bit_extender_1
  Adder #(.width(32)) adder_1 (.a(base), .b(bit_extender_1_out), .out(adder_1_out));  // open: cin, cout
  Bit_Extender #(.in_width(32)) bit_extender_2 (.in(adder_1_out), .out(addr));
endmodule

module MuxGRFAddr (
  input  saveRt,
  input  [4:0] Rd,
  input  [4:0] Rs,
  input  [4:0] Rt,
  output [4:0] GFRAddrIn,
  output [4:0] GRFAddrOut1,
  output [4:0] GRFAddrOut2
);

  Multiplexer #(.width(5)) multiplexer_1 (.in0(Rd), .in1(Rt), .out(GFRAddrIn), .sel(saveRt));  // open: en

  assign GRFAddrOut1 = Rs;
  assign GRFAddrOut2 = Rt;
endmodule

module MuxALU (
  input  ALUimm,
  input  [31:0] Rs,
  input  [31:0] Rt,
  input  [15:0] imm,
  output [31:0] Operand1,
  output [31:0] Operand2
);

  wire [31:0] bit_extender_1_out;

  assign bit_extender_1_out = {{16{1'b0}}, imm};  // Bit_Extender bit_extender_1
  Multiplexer #(.width(32)) multiplexer_1 (
    .in0(Rt), .in1(bit_extender_1_out), .out(Operand2), .sel(ALUimm));  // open: en

  assign Operand1 = Rs;
endmodule

module cpu (
  input  reset
);

  wire ALU2Reg, alu_1_eq, alu_1_gt, alu_1_lt, ALUimm, beq, clk, controller_1_regwrite, controller_1_savert,
       imm2Reg, jflag, Mem2Reg, MemLoad, MemWrite;
  wire [1:0] ALUop;
  wire [4:0] controller_1_rd, controller_1_rs, controller_1_rt, muxgrfaddr_1_gfraddrin,
       muxgrfaddr_1_grfaddrout1, muxgrfaddr_1_grfaddrout2;
  wire [5:0] func, op;
  wire [15:0] addr16;
  wire [25:0] addr26;
  wire [31:0] ALUout, ifu_1_instruct, MemOut, mux2reg_1_out_7, muxalu_1_operand1, muxalu_1_operand2, RsOut,
       RtOut;

  Clock clock_1 (.out(clk));
  IFU ifu_1 (.offset(addr16), .jflag(jflag), .clk(clk), .reset(reset), .instruct(ifu_1_instruct));  // open: PC
  Mux2Reg mux2reg_1 (
    .ALUout(ALUout), .ALU2Reg(ALU2Reg), .Memout(MemOut), .Mem2Reg(Mem2Reg), .immout(addr16),
    .imm2Reg(imm2Reg), .out_7(mux2reg_1_out_7));
  Controller controller_1 (
    .\input (ifu_1_instruct), .op(op), .Rs(controller_1_rs), .Rt(controller_1_rt), .Rd(controller_1_rd),
    .func(func), .addr16(addr16), .addr26(addr26), .ALUop(ALUop), .RegWrite(controller_1_regwrite),
    .MemWrite(MemWrite), .MemLoad(MemLoad), .ALU2Reg(ALU2Reg), .Mem2Reg(Mem2Reg), .imm2Reg(imm2Reg),
    .beq(beq), .saveRt(controller_1_savert), .ALUimm(ALUimm));  // open: Shamt
  MuxGRFAddr muxgrfaddr_1 (
    .Rd(controller_1_rd), .Rs(controller_1_rs), .Rt(controller_1_rt), .saveRt(controller_1_savert),
    .GFRAddrIn(muxgrfaddr_1_gfraddrin), .GRFAddrOut1(muxgrfaddr_1_grfaddrout1),
    .GRFAddrOut2(muxgrfaddr_1_grfaddrout2));
  GRF grf_1 (
    .RegWrite(controller_1_regwrite), .RegData(mux2reg_1_out_7), .RegAddrIn(muxgrfaddr_1_gfraddrin),
    .AddrOut1(muxgrfaddr_1_grfaddrout1), .AddrOut2(muxgrfaddr_1_grfaddrout2), .clk(clk), .in_7(reset),
    .Out1(RsOut), .Out2(RtOut));
  MuxALU muxalu_1 (
    .Rs(RsOut), .Rt(RtOut), .imm(addr16), .ALUimm(ALUimm), .Operand1(muxalu_1_operand1),
    .Operand2(muxalu_1_operand2));
  DM dm_1 (
    .base(RsOut), .offset(addr16), .\input (RtOut), .MemWrite(MemWrite), .clk(clk), .MemLoad(MemLoad),
    .reset(reset), .\output (MemOut));  // open: MemAddr
  ALU alu_1 (
    .op(ALUop), .operand1(muxalu_1_operand1), .operand2(muxalu_1_operand2), .ALUout(ALUout), .gt(alu_1_gt),
    .eq(alu_1_eq), .lt(alu_1_lt));
  comp2jflag comp2jflag_1 (.beq(beq), .gt(alu_1_gt), .eq(alu_1_eq), .lt(alu_1_lt), .jflag(jflag));
endmodule
